# Fritzing sketch electronicsetup (saved by Fritzing 0.9.0b)

parts:
  Part1 = EasyDriver_v44  # not connected
  Part2 = EasyDriver_v44  # not connected
  Part3 = EasyDriver_v44
  Part4 = EasyDriver_v44  # not connected
  Part5 = EasyDriver_v44
  Part6 = EasyDriver_v44
  Teensy_3_1 = Teensy 3.1  # not connected
  Teensy_3_2 = Teensy 3.1
  M2 = Stepper Motor - Bipolar
  M3 = Stepper Motor - Bipolar
  M4 = Stepper Motor - Bipolar  # not connected
  M5 = Stepper Motor - Bipolar  # not connected
  M6 = Stepper Motor - Bipolar  # not connected
  M1 = Stepper Motor - Bipolar

nets:
  GND: Part3.GND, Teensy_3_2.GND
  N1: Part3.STEP, Teensy_3_2.D3
  N2: Part3.DIR, Teensy_3_2.D2
  N3: Part3.OUT2A, M1.A
  N4: Part3.OUT2B, M1.C
  N5: Part3.OUT1A, M1.B
  N6: Part3.OUT1B, M1.D
  VCC: Part3.VCC, Teensy_3_2.Vin
  N7: Part3.MS1, Teensy_3_2.D7
  N8: Part3.ENABLE, Teensy_3_2.D5
  N9: Part3.MS2, Teensy_3_2.D4
  N10: Part5.OUT2A, M3.A
  N11: Part5.OUT2B, M3.C
  N12: Part5.OUT1A, M3.B
  N13: Part5.OUT1B, M3.D
  N14: Part6.STEP, Teensy_3_2.D11
  N15: Part6.DIR, Teensy_3_2.D6
  N16: Part6.OUT2A, M2.A
  N17: Part6.OUT2B, M2.C
  N18: Part6.OUT1A, M2.B
  N19: Part6.OUT1B, M2.D
